// Digital circuit MUX.dig as structural Verilog
module MUX (
  input  [2:0] D,
  input  C,
  input  B,
  input  A,
  output Y
);

  // Not not_1 is placed but not wired
  Multiplexer #(.Selector_Bits(3)) multiplexer_1 (
    .sel({A, B, C}), .in_1(C), .in_2(C), .in_3(C), .in_4(C), .in_5(C), .in_6(C), .in_7(C), .out(Y));  // open: in_0
  // Pins of 1 and 3 bits meet at {A, B, C}

  assign D = {A, B, C};

  // Notes on the sheet:
  //   Use A as the most-significant bit and 
  //   D as the least-significant bit.
  //   Converts between single bits & a 3-bit bus
endmodule

/* Test case:
A B C D Y
0 0 0 0 X
0 0 0 1 1
*/
